# Fritzing sketch Untitled Sketch 2 (saved by Fritzing 0.9.3b)
breadboards: 1

parts:
  元件1 = Arduino Uno (Rev3)
  RHT1 = Humidity and Temperature Sensor RHT03
  S2 = Toggle Switch spst [package=THT]
  元件2 = HC-SR501 Body Sensor Module
  U2 = L9110 H-bridge module [part_number="L9110 H-bridge"]
  WATER_PUMP1 = water pump/motor  # not connected
  U3 = WS2812 RGB LED matrix 1x8

nets:
  N1: 元件1.D2, RHT1.Data-signal
  N2: 元件1.D3_PWM, 元件2.OUT
  N3: 元件1.D4, U2.A-IB
  N4: 元件1.D7, U3.DIN
  N5: 元件1.5V, S2.COM
  GND: 元件1.GND, RHT1.GND_2, 元件2.GND, U2.GND, U2.A-IA, U3.GND
  VCC: RHT1.Vcc, S2.L1, 元件2.VCC, U2.VCC, U3.VCC

custom parts:
  Toggle Switch spst: Toggle Switch single pole single throw
  HC-SR501 Body Sensor Module: Pyroelectric Infrared PIR Motion Sensor Detector Module
  water pump/motor: WATER PUMP BY ARDUBLOCKTR
  WS2812 RGB LED matrix 1x8: WS2812 matrix 1x8
